# Fritzing sketch прототип1_игумнов (saved by Fritzing 0.9.3b)
breadboards: 2

parts:
  Часть1 = Arduino Uno (Rev3)
  VCC1 = Battery
  S1 = Pushbutton [package="[THT]"]
  S2 = Pushbutton [package="[THT]"]
  S3 = Pushbutton [package="[THT]"]
  Disp1 = LBT2088AH [part_number=LBT2088AH]
  7_Segment1 = 7 Segment Display
  7_Segment2 = 7 Segment Display  # not connected
  7_Segment3 = 7 Segment Display  # not connected
  7_Segment4 = 7 Segment Display  # not connected
  S4 = Toggle Switch [package=THT]
  RE1 = Rotary Encoder [package=THT]  # not connected

nets:
  N1: Часть1.D2, Disp1.pin_5
  N2: Часть1.D3_PWM, S1.Pin_3, S1.Pin_4
  N3: Часть1.D4, S2.Pin_3, S2.Pin_4
  N4: Часть1.D5_PWM, S3.Pin_3, S3.Pin_4
  N5: Часть1.D6_PWM, 7_Segment1.Segment_E
  N6: VCC1.-, S4.L1
  N7: VCC1.+, Disp1.pin_3, Disp1.pin_4, 7_Segment1.Segment_F
  N8: S1.Pin_1, S1.Pin_2, S2.Pin_1, S2.Pin_2, S3.Pin_1, S3.Pin_2, Disp1.pin_6, 7_Segment1.common_anode, S4.L2
